# Fritzing sketch batteries (saved by Fritzing 0.9.3b)

parts:
  BAT1 = Battery Holders [package=battery-aa-kit]
  BAT2 = Battery Holders [package=battery-aa-kit]
  BAT3 = Battery Holders [package=battery-aa-kit]
  BAT4 = Battery Holders [package=battery-aa-kit]
  BAT5 = Battery Holders [package=battery-aa-kit]
  BAT6 = Battery Holders [package=battery-aa-kit]
  BAT7 = Battery Holders [package=battery-aa-kit]
  BAT8 = Battery Holders [package=battery-aa-kit]
  BAT9 = Battery Holders [package=battery-aa-kit]
  BAT10 = Battery Holders [package=battery-aa-kit]
  M1 = RioRand LM2596
  Power_plug1 = Power plug
  Power_plug2 = Power plug

nets:
  N1: BAT1.+, BAT2.-
  N2: BAT1.-, BAT9.-, M1.Pin_1, Power_plug2.GND
  N3: BAT2.+, BAT3.-
  N4: BAT3.+, BAT4.-
  N5: BAT4.+, BAT5.-
  N6: BAT5.+, BAT10.+, M1.Pin_2, Power_plug2.VCC
  N7: BAT6.+, BAT10.-
  N8: BAT6.-, BAT8.+
  N9: BAT7.+, BAT8.-
  N10: BAT7.-, BAT9.+
  N11: M1.Pin_3, Power_plug1.GND
  N12: M1.Pin_4, Power_plug1.VCC

notes:
  ~7V
  5V
