# Fritzing sketch connections (saved by Fritzing 0.9.3b)

parts:
  MCU1 = Raspberry Pi Zero
  J1 = Basic Servo
  Part3 = 16-Channel 12-bit PWM Servo Driver - I2C [part_number=815]
  J2 = Basic Servo
  Power_plug1 = Power plug
  Power_plug2 = Power plug
  M3 = DC Motor
  M4 = DC Motor
  Part4 = Motor Driver 1A Dual TB6612FNG
  M2 = DC Motor
  M1 = DC Motor
  Part5 = 16-Channel 12-bit PWM Servo Driver - I2C [part_number=815]  # not connected

nets:
  VCC: MCU1.pin_2, MCU1.pin_4, Part3.VCC, Power_plug1.VCC, Part4.VCC, Part4.STBY
  N1: MCU1.pin_3, Part3.SDA
  N2: MCU1.pin_5, Part3.SCL
  GND: MCU1.pin_6, MCU1.pin_9, J1.gnd, Part3.GND, J2.gnd, Power_plug1.GND, Power_plug2.GND, Part4.GND
  N3: MCU1.pin_16, Part4.BIN2
  N4: MCU1.pin_18, Part4.BIN1
  N5: MCU1.pin_22, Part4.AIN1
  N6: MCU1.pin_24, Part4.AIN2
  VCC_2: J1.vcc, Part3.5.0V, J2.vcc, Power_plug2.VCC, Part4.VM
  N7: J1.pulse, Part3.PWM0
  N8: Part3.PWM1, J2.pulse
  N9: Part3.PWM15, Part4.PWMB
  N10: Part3.PWM14, Part4.PWMA
  N11: M3.pin_1, M4.pin_1, Part4.A01
  N12: M3.pin_2, M4.pin_2, Part4.A02
  N13: Part4.B01, M2.pin_2, M1.pin_2
  N14: Part4.B02, M2.pin_1, M1.pin_1

notes:
  +5V
  +6V

custom parts:
  16-Channel 12-bit PWM Servo Driver - I2C: You want to make a cool robot, maybe a hexapod walker, or maybe just a piece of art with a lot of moving parts. Or maybe you want to drive a lot of LEDs with precise PWM output. Using only two pins, control 16 free-running PWM outputs! You can even chain up 62 breakouts to control up to 992 PWM outputs.
