# Fritzing sketch lipo (saved by Fritzing 0.9.3b)

parts:
  M1 = RioRand LM2596
  Power_plug1 = Power plug
  Power_plug2 = Power plug
  M2 = RioRand LM2596
  Power_plug3 = Power plug
  U1 = LIPO-2000mAh [package=lipo-2000]

nets:
  N1: M1.Pin_1, M2.Pin_1, Power_plug3.VCC, U1.-
  N2: M1.Pin_3, Power_plug1.GND
  N3: M1.Pin_4, Power_plug1.VCC
  N4: Power_plug2.GND, M2.Pin_4
  N5: Power_plug2.VCC, M2.Pin_3

notes:
  6V
  5V
  7.2V
