# Fritzing sketch connections (saved by Fritzing 0.9.3b)

parts:
  MCU1 = Raspberry Pi Zero
  J1 = Basic Servo
  Part3 = 16-Channel 12-bit PWM Servo Driver - I2C [part_number=815]
  J2 = Basic Servo
  Power_plug1 = Power plug
  Power_plug2 = Power plug  # not connected
  Part4 = Logic Level Converter
  R1 = Resistor [tolerance=±5% resistance=220 package="0603 [SMD]"]
  Q1 = npn-Powertransistor [package="TO220 [THT]"]
  R2 = Resistor [tolerance=±5% resistance=12 power=2W package="0805 [SMD]"]
  LED1 = LEDs [package=led10mm]

nets:
  N1: MCU1.pin_1, MCU1.pin_17, Part4.LV, Part4.RX_LV
  VCC: MCU1.pin_2, J1.vcc, Part3.5.0V, Part3.VCC, J2.vcc, Power_plug1.VCC, Part4.RX_HV, Part4.HV, LED1.C
  N2: MCU1.pin_3, Part3.SDA
  N3: MCU1.pin_5, Part3.SCL
  GND: MCU1.pin_6, MCU1.pin_9, J1.gnd, Part3.GND, J2.gnd, Power_plug1.GND, Part4.GND, Q1.emitter
  N4: MCU1.pin_35, Part4.TX_LV
  N5: J1.pulse, Part3.PWM0
  N6: Part3.PWM1, J2.pulse
  N7: Part4.TX_HV, R1.Pin_0
  N8: R1.Pin_1, Q1.base
  N9: Q1.collector, R2.Pin_0
  N10: R2.Pin_1, LED1.A

notes:
  +5V
  optional to power also Rpi
  +5V ( No need if we power Rpi through PowerPin)

custom parts:
  16-Channel 12-bit PWM Servo Driver - I2C: You want to make a cool robot, maybe a hexapod walker, or maybe just a piece of art with a lot of moving parts. Or maybe you want to drive a lot of LEDs with precise PWM output. Using only two pins, control 16 free-running PWM outputs! You can even chain up 62 breakouts to control up to 992 PWM outputs.
