# Fritzing sketch justservo (saved by Fritzing 0.9.3b)

parts:
  MCU1 = Raspberry Pi Zero
  J1 = Basic Servo
  Part3 = 16-Channel 12-bit PWM Servo Driver - I2C [part_number=815]
  J2 = Basic Servo
  Power_plug1 = Power plug
  Power_plug2 = Power plug  # not connected

nets:
  N1: MCU1.pin_3, Part3.SDA
  N2: MCU1.pin_5, Part3.SCL
  GND: MCU1.pin_6, MCU1.pin_9, J1.gnd, Part3.GND, J2.gnd, Power_plug1.GND
  VCC: J1.vcc, Part3.5.0V, Part3.VCC, J2.vcc, Power_plug1.VCC
  N3: J1.pulse, Part3.PWM0
  N4: Part3.PWM1, J2.pulse

notes:
  +5V

custom parts:
  16-Channel 12-bit PWM Servo Driver - I2C: You want to make a cool robot, maybe a hexapod walker, or maybe just a piece of art with a lot of moving parts. Or maybe you want to drive a lot of LEDs with precise PWM output. Using only two pins, control 16 free-running PWM outputs! You can even chain up 62 breakouts to control up to 992 PWM outputs.
