# Fritzing sketch schematic (saved by Fritzing 0.9.3b)

parts:
  MCU1 = Raspberry Pi Zero
  S1 = Round Pushbutton
  R1 = Resistor [tolerance=±5% resistance=220 package="0603 [SMD]"]
  LED1 = smd LED [color="Red (633nm)" package="1206 [SMD]"]

nets:
  N1: MCU1.pin_35, LED1.anode
  N2: MCU1.pin_37, S1.leg1
  N3: MCU1.pin_39, S1.leg0
  N4: R1.Pin_0, LED1.cathode
