# Fritzing sketch schematic (saved by Fritzing 0.9.3b)
breadboards: 1

parts:
  BAT1 = Battery Holders [package=battery-aa-kit]
  BAT2 = Battery Holders [package=battery-aa-kit]
  BAT3 = Battery Holders [package=battery-aa-kit]
  BAT4 = Battery Holders [package=battery-aa-kit]
  BAT5 = Battery Holders [package=battery-aa-kit]
  BAT6 = Battery Holders [package=battery-aa-kit]
  BAT7 = Battery Holders [package=battery-aa-kit]
  BAT8 = Battery Holders [package=battery-aa-kit]
  BAT9 = Battery Holders [package=battery-aa-kit]
  BAT10 = Battery Holders [package=battery-aa-kit]
  M1 = RioRand LM2596
  WeMos_D1_Mini1 = WeMos D1 Mini  # not connected
  M5 = DC Motor
  M6 = DC Motor
  M7 = DC Motor
  M8 = DC Motor
  Part5 = Motor Driver 1A Dual TB6612FNG
  Part6 = Logic Level Converter Bi-Directional BOB-12009
  NEOPIXEL1 = Neopixel Strip -- White (60/m)
  R1 = Resistor [tolerance=±5% resistance=220 package="2010 [SMD]"]

nets:
  N1: BAT1.+, BAT2.-
  N2: BAT1.-, BAT9.-, M1.Pin_2
  N3: BAT2.+, BAT3.-
  N4: BAT3.+, BAT4.-
  N5: BAT4.+, BAT5.-
  N6: BAT5.+, BAT10.+, M1.Pin_1, Part5.VM
  N7: BAT6.+, BAT10.-
  N8: BAT6.-, BAT8.+
  N9: BAT7.+, BAT8.-
  N10: BAT7.-, BAT9.+
  N11: M1.Pin_3, Part6.HV, NEOPIXEL1.DI
  GND: M1.Pin_4, Part5.GND, Part6.GND, NEOPIXEL1.GND, R1.Pin_1
  N12: M5.pin_1, M6.pin_1, Part5.A01
  N13: M5.pin_2, M6.pin_2, Part5.A02
  N14: M7.pin_1, M8.pin_1, Part5.B02
  N15: M7.pin_2, M8.pin_2, Part5.B01
  N16: Part5.VCC, Part6.LV
  N17: Part6.HV1, NEOPIXEL1.+5V, R1.Pin_0

notes:
  <--- 3.3V
  <-- 5.0V
  LEFT SIDE
  RIGHT SIDE
  5.0V
  GND
  ~6.8k

custom parts:
  Logic Level Converter Bi-Directional BOB-12009: SparkFun product BOB-12009 If you’ve ever tried to connect a 3.3V device to a 5V system, you know what a challenge it can be. The SparkFun bi-directional logic level converter is a small device that safely steps down 5V signals to 3.3V AND steps up 3.3V to 5V at the same time. This level converter also works with 2.8V and 1.8V devices. What really separates this Logic level converter from our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
  Neopixel Strip -- White (60/m): Neopixel Strip, White, 60 pixels per meter.
