# Fritzing sketch schematic (saved by Fritzing 0.9.3b)
breadboards: 1

parts:
  BAT1 = Battery Holders [package=battery-aa-kit]
  BAT2 = Battery Holders [package=battery-aa-kit]
  BAT3 = Battery Holders [package=battery-aa-kit]
  BAT4 = Battery Holders [package=battery-aa-kit]
  BAT5 = Battery Holders [package=battery-aa-kit]
  BAT6 = Battery Holders [package=battery-aa-kit]
  BAT7 = Battery Holders [package=battery-aa-kit]
  BAT8 = Battery Holders [package=battery-aa-kit]
  BAT9 = Battery Holders [package=battery-aa-kit]
  BAT10 = Battery Holders [package=battery-aa-kit]
  WeMos_D1_Mini1 = WeMos D1 Mini
  M5 = DC Motor
  M6 = DC Motor
  M7 = DC Motor
  M8 = DC Motor
  Part5 = Motor Driver 1A Dual TB6612FNG

nets:
  N1: BAT1.+, BAT2.-
  N2: BAT1.-, BAT9.-, Part5.GND
  N3: BAT2.+, BAT3.-
  N4: BAT3.+, BAT4.-
  N5: BAT4.+, BAT5.-
  N6: BAT6.+, BAT10.-
  N7: BAT6.-, BAT8.+
  N8: BAT7.+, BAT8.-
  N9: BAT7.-, BAT9.+
  N10: WeMos_D1_Mini1.5V, Part5.VM
  N11: M5.pin_1, M6.pin_1, Part5.A01
  N12: M5.pin_2, M6.pin_2, Part5.A02
  N13: M7.pin_1, M8.pin_1, Part5.B02
  N14: M7.pin_2, M8.pin_2, Part5.B01

notes:
  LEFT SIDE
  RIGHT SIDE
