# Fritzing sketch schematics (saved by Fritzing 0.9.3b)
breadboards: 1

parts:
  U1 = NodeMCU V3.0
  S1 = Momentary Switch [package=ksa_sealed_tac_switch]
  LED1 = LED - 5mm [color="Red (633nm)" package="5 mm [THT]"]
  R1 = Resistor [tolerance=±5% resistance=220 package="0805 [SMD]"]

nets:
  N1: U1.D2, S1.4
  N2: U1.GND#6, U1.GND#13, U1.GND#16, U1.GND#33, S1.2, R1.Pin_1
  N3: U1.D5, LED1.cathode
  N4: LED1.anode, R1.Pin_0

custom parts:
  NodeMCU V3.0: ESP8266 based NodeMCU
