# Fritzing sketch schematicsRpi (saved by Fritzing 0.9.3b)
breadboards: 1

parts:
  S1 = Momentary Switch [package=ksa_sealed_tac_switch]
  LED1 = LED - 5mm [color="Red (633nm)" package="5 mm [THT]"]
  R1 = Resistor [tolerance=±5% resistance=220 package="0805 [SMD]"]
  MCU1 = Raspberry Pi Zero

nets:
  N1: S1.2, MCU1.pin_1, MCU1.pin_17
  N2: S1.4, MCU1.pin_37
  N3: LED1.cathode, MCU1.pin_35
  N4: LED1.anode, R1.Pin_0
  N5: R1.Pin_1, MCU1.pin_9, MCU1.pin_39
