# Fritzing sketch connections (saved by Fritzing 0.9.3b)
breadboards: 1

parts:
  U1 = NodeMCU V3.0
  Part3 = 16 NeoPixel Ring [part_number=1463]
  Part4 = Logic Level Converter Bi-Directional BOB-12009
  DFRobot_DFPlayer_Mini1 = DFRobot DFPlayer Mini [part_number=DFR0299]
  Part5 = 16 NeoPixel Ring [part_number=1463]
  SP1 = SPEAKER [package=pcb_mount_speaker]

nets:
  N1: U1.D3, Part4.LV1
  N2: U1.D4, Part4.LV2
  N3: U1.3V3, Part4.LV
  GND: U1.GND#6, U1.GND#13, U1.GND#16, U1.GND#33, Part3.GND, Part4.GND, DFRobot_DFPlayer_Mini1.GND-1, DFRobot_DFPlayer_Mini1.GND-2, Part5.GND
  N4: U1.D5, Part4.LV3
  N5: U1.D6, Part4.LV4
  VDD: U1.Vin, Part3.VDD, Part4.HV, DFRobot_DFPlayer_Mini1.VCC, Part5.VDD
  N6: Part3.IN, Part4.HV3
  N7: Part4.HV1, DFRobot_DFPlayer_Mini1.RX
  N8: Part4.HV2, DFRobot_DFPlayer_Mini1.TX
  N9: Part4.HV4, Part5.IN
  N10: DFRobot_DFPlayer_Mini1.SPK_1, SP1.+
  N11: DFRobot_DFPlayer_Mini1.SPK_2, SP1.-

custom parts:
  NodeMCU V3.0: ESP8266 based NodeMCU
  16 NeoPixel Ring: 16 ultra bright smart LED NeoPixels are arranged in a circle with 1.75" (44.5mm) outer diameter. The rings are 'chainable' - connect the output pin of one to the input pin of another. Use only one microcontroller pin to control as many as you can chain together! Each LED is addressable as the driver chip is inside the LED. Each one has ~18mA constant current drive so the color will be very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
  Logic Level Converter Bi-Directional BOB-12009: SparkFun product BOB-12009 If you’ve ever tried to connect a 3.3V device to a 5V system, you know what a challenge it can be. The SparkFun bi-directional logic level converter is a small device that safely steps down 5V signals to 3.3V AND steps up 3.3V to 5V at the same time. This level converter also works with 2.8V and 1.8V devices. What really separates this Logic level converter from our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
