# Fritzing sketch schematics (saved by Fritzing 0.9.3b)
breadboards: 1

parts:
  U1 = NodeMCU V3.0
  S1 = Momentary Switch [package=ksa_sealed_tac_switch]
  LED1 = LED - 5mm [color="Red (633nm)" package="5 mm [THT]"]
  R1 = Resistor [tolerance=±5% resistance=220 package="0805 [SMD]"]
  U2 = ENCODER-QUADRATURE [package=encoder-16mm-quad]
  LCD2 = LCD screen
  LCM1602_IIC1 = LCM1602 IIC [part_number="LCM1602 IIC" chip_label="LCM1602 IIC" package="DIP (Dual Inline) [THT]"]
  R2 = Rotary Potentiometer (Small) [maximum_resistance=100kΩ package=THT]
  J1 = Basic Servo

nets:
  N1: U1.D1, LCM1602_IIC1.SCL
  N2: U1.D2, LCM1602_IIC1.SDA
  N3: U1.D3, LED1.cathode
  N4: U1.3V3, R2.leg2
  GND: U1.GND#6, U1.GND#13, U1.GND#16, U1.GND#33, S1.1, R1.Pin_1, U2.C, LCM1602_IIC1.GND, R2.leg1, J1.gnd
  N5: U1.D5, U2.B
  N6: U1.D6, U2.A
  N7: U1.D7, S1.4
  N8: U1.D8, J1.pulse
  VCC: U1.Vin, LCM1602_IIC1.VCC, J1.vcc
  N9: U1.A0, R2.wiper
  N10: LED1.anode, R1.Pin_0
  VSS: LCD2.VSS, LCM1602_IIC1.VSS
  VDD: LCD2.VDD, LCM1602_IIC1.VDD
  N11: LCD2.V0, LCM1602_IIC1.V0
  N12: LCD2.RS, LCM1602_IIC1.RS
  N13: LCD2.R/W, LCM1602_IIC1.RW
  N14: LCD2.E, LCM1602_IIC1.E
  N15: LCD2.DB0, LCM1602_IIC1.D0
  N16: LCD2.DB1, LCM1602_IIC1.D1
  N17: LCD2.DB2, LCM1602_IIC1.D2
  N18: LCD2.DB3, LCM1602_IIC1.D3
  N19: LCD2.DB4, LCM1602_IIC1.D4
  N20: LCD2.DB5, LCM1602_IIC1.D5
  N21: LCD2.DB6, LCM1602_IIC1.D6
  N22: LCD2.DB7, LCM1602_IIC1.D7
  N23: LCD2.LED+, LCM1602_IIC1.A
  N24: LCD2.LED-, LCM1602_IIC1.K
  N25: LCM1602_IIC1.LED_A, LCM1602_IIC1.LED_B

custom parts:
  NodeMCU V3.0: ESP8266 based NodeMCU
  LCM1602 IIC: I2C-Module to use a 1602 or 2004 LCD on with the wire.h libory Serial LCD Modul
