# Fritzing sketch connections (saved by Fritzing 0.9.3b)

parts:
  WeMos_D1_Mini1 = WeMos D1 Mini
  U1 = NodeMCU V3.0
  Part1 = BME280 Breakout
  Part2 = BME280 Breakout

nets:
  3V3: WeMos_D1_Mini1.3V3, Part2.3.3V
  N1: WeMos_D1_Mini1.D0, WeMos_D1_Mini1.RST
  N2: WeMos_D1_Mini1.D1, Part2.SCK/SCL
  N3: WeMos_D1_Mini1.D2, Part2.SDI/SDA
  N4: WeMos_D1_Mini1.G, Part2.GND
  N5: U1.D0, U1.RST
  N6: U1.D1, Part1.SCK/SCL
  N7: U1.D2, Part1.SDI/SDA
  3V3_2: U1.3V3, Part1.3.3V
  GND: U1.GND, Part1.GND

custom parts:
  NodeMCU V3.0: ESP8266 based NodeMCU
