# Fritzing sketch connections (saved by Fritzing 0.9.3b)

parts:
  WeMos_D1_Mini1 = WeMos D1 Mini
  U1 = NodeMCU V3.0
  LED2 = RGB LED (com. anode, rbg) [package="5 mm [THT]"]
  LED3 = LED - 3mm [color="Red (633nm)" package="3 mm [THT]"]
  LED4 = LED - 3mm [color="Red (633nm)" package="3 mm [THT]"]
  S1 = Round Pushbutton
  S2 = Round Pushbutton
  R1 = Resistor [tolerance=±5% resistance=220 package="2010 [SMD]"]  # not connected
  R3 = Resistor [tolerance=±5% resistance=220 package="2010 [SMD]"]
  R4 = Resistor [tolerance=±5% resistance=220 package="2010 [SMD]"]
  R2 = Resistor [tolerance=±5% resistance=220 package="2010 [SMD]"]
  R5 = Resistor [tolerance=±5% resistance=220 package="2010 [SMD]"]

nets:
  N1: WeMos_D1_Mini1.3V3, LED2.common_anode
  N2: WeMos_D1_Mini1.D1, LED4.cathode
  N3: WeMos_D1_Mini1.D5, R4.Pin_1
  N4: WeMos_D1_Mini1.D6, R3.Pin_1
  N5: WeMos_D1_Mini1.D7, R2.Pin_1
  N6: WeMos_D1_Mini1.G, R5.Pin_1
  N7: U1.D1, S1.leg0
  N8: U1.D2, S2.leg0
  N9: U1.D5, LED3.cathode
  N10: U1.GND, S1.leg1, S2.leg1

custom parts:
  NodeMCU V3.0: ESP8266 based NodeMCU
