# Fritzing sketch schematic (saved by Fritzing 0.9.3b)

parts:
  WeMos_D1_Mini1 = WeMos D1 Mini
  hc-sr1 = hc-sr04

nets:
  5V: WeMos_D1_Mini1.5V, hc-sr1.VCC
  N1: WeMos_D1_Mini1.D2, hc-sr1.Echo
  N2: WeMos_D1_Mini1.D3, hc-sr1.Trig
  N3: WeMos_D1_Mini1.G, hc-sr1.GND
